// Logisim project Ctl_Shift_Add_Sub_Mov.circ as structural Verilog: 1 circuit, main circuit Shift_Add_Sub_Mov
module Shift_Add_Sub_Mov (
  input  Enable,
  input  [15:0] Instruction,
  output [3:0] Flags_Update_Mask,
  output Carry,
  output Imm32_Enable,
  output [2:0] Rm,
  output [2:0] Rn,
  output [2:0] Rd,
  output [4:0] Imm5,
  output [31:0] Imm32,
  output [3:0] ALU_Opcode
);

  wire and_5_out, and_6_out, and_7_out, and_8_out, bit_sortant_decallage_left_logic,
       bit_sortant_decallage_right_logic, Logical_Shift_Left_bool, Logical_Shift_Right_bool;
  wire [1:0] bit_extender_4_out, bit_extender_5_out, bit_extender_6_out, bit_extender_7_out;
  wire [2:0] and_1_out, and_2_out, bit_extender_10_out, bit_extender_11_out, bit_extender_12_out,
       bit_extender_13_out, bit_extender_14_out, bit_extender_15_out, left_logical_shift_output,
       right_logical_shift_output, Rm_Value;
  wire [4:0] bit_extender_1_out, bit_extender_2_out, imm5_Value, subtractor_1_out, subtractor_2_out;
  wire [5:0] bitselector_2_out;
  wire [10:0] bitselector_3_out, bitselector_4_out;
  wire [31:0] bit_extender_8_out, bit_extender_9_out, shifter_1_out, shifter_2_out;

  BitSelector #(.group(3), .width(16)) bitselector_1 (.in(Instruction), .out(Rm_Value), .sel(3'b001));
  BitSelector #(.group(6), .width(16)) bitselector_2 (.in(Instruction), .out(bitselector_2_out), .sel(2'b01));
  BitSelector #(.group(11), .width(16)) bitselector_3 (.in(Instruction), .out(bitselector_3_out), .sel(1'b1));
  BitSelector #(.group(11), .width(16)) bitselector_4 (.in(Instruction), .out(bitselector_4_out), .sel(1'b1));
  assign bit_extender_1_out = {{2{1'b0}}, 3'b011};  // Bit_Extender bit_extender_1
  assign bit_extender_2_out = {{2{1'b0}}, 3'b001};  // Bit_Extender bit_extender_2
  Bit_Extender #(.in_width(6), .out_width(5)) bit_extender_3 (.in(bitselector_2_out), .out(imm5_Value));
  Bit_Extender #(.in_width(11), .out_width(2)) bit_extender_4 (.in(bitselector_3_out), .out(bit_extender_4_out));
  Bit_Extender #(.in_width(11), .out_width(2)) bit_extender_5 (.in(bitselector_4_out), .out(bit_extender_5_out));
  Bit_Extender #(.in_width(5), .out_width(2)) bit_extender_6 (.in(subtractor_1_out), .out(bit_extender_6_out));
  Subtractor #(.width(5)) subtractor_1 (
    .a(bit_extender_1_out), .b(imm5_Value), .out(subtractor_1_out));  // open: bin, bout
  Bit_Extender #(.in_width(5), .out_width(2)) bit_extender_7 (.in(subtractor_2_out), .out(bit_extender_7_out));
  Subtractor #(.width(5)) subtractor_2 (
    .a(imm5_Value), .b(bit_extender_2_out), .out(subtractor_2_out));  // open: bin, bout
  BitSelector #(.width(3)) bitselector_5 (
    .in(Rm_Value), .out(bit_sortant_decallage_left_logic), .sel(bit_extender_6_out));
  BitSelector #(.width(3)) bitselector_6 (
    .in(Rm_Value), .out(bit_sortant_decallage_right_logic), .sel(bit_extender_7_out));
  Comparator #(.width(2)) comparator_1 (
    .a(bit_extender_4_out), .b(2'b00), .eq(Logical_Shift_Left_bool));  // open: gt, lt
  Comparator #(.width(2)) comparator_2 (
    .a(bit_extender_5_out), .b(2'b01), .eq(Logical_Shift_Right_bool));  // open: gt, lt
  assign bit_extender_8_out = {{29{Rm_Value[2]}}, Rm_Value};  // Bit_Extender bit_extender_8
  assign bit_extender_9_out = {{29{Rm_Value[2]}}, Rm_Value};  // Bit_Extender bit_extender_9
  Shifter #(.width(32)) shifter_1 (.in(bit_extender_8_out), .\dist (imm5_Value), .out(shifter_1_out));
  Bit_Extender #(.in_width(32), .out_width(3)) bit_extender_10 (.in(shifter_1_out), .out(bit_extender_10_out));
  Bit_Extender #(.in_width(32), .out_width(3)) bit_extender_11 (.in(shifter_2_out), .out(bit_extender_11_out));
  Shifter #(.shift("lr"), .width(32)) shifter_2 (.in(bit_extender_9_out), .\dist (imm5_Value), .out(shifter_2_out));
  assign bit_extender_12_out = {{2{Logical_Shift_Left_bool}}, Logical_Shift_Left_bool};  // Bit_Extender bit_extender_12
  assign and_1_out = bit_extender_12_out & bit_extender_10_out;  // AND_Gate and_1, 3 bits wide
  assign bit_extender_13_out = {{2{Logical_Shift_Right_bool}}, Logical_Shift_Right_bool};  // Bit_Extender bit_extender_13
  assign Rd = left_logical_shift_output | right_logical_shift_output;  // OR_Gate or_1, 3 bits wide
  assign and_2_out = bit_extender_13_out & bit_extender_11_out;  // AND_Gate and_2, 3 bits wide
  assign bit_extender_14_out = {{2{Enable}}, Enable};  // Bit_Extender bit_extender_14
  assign left_logical_shift_output = bit_extender_14_out & and_1_out;  // AND_Gate and_3, 3 bits wide
  assign bit_extender_15_out = {{2{Enable}}, Enable};  // Bit_Extender bit_extender_15
  assign right_logical_shift_output = bit_extender_15_out & and_2_out;  // AND_Gate and_4, 3 bits wide
  Comparator #(.width(3)) comparator_3 (.a(Rd), .b(3'b000), .lt(Flags_Update_Mask[3]));  // open: gt, eq
  Comparator #(.width(3)) comparator_4 (.a(Rd), .b(3'b000), .eq(Flags_Update_Mask[2]));  // open: gt, lt
  and and_5 (and_5_out, Logical_Shift_Left_bool, 1'b1);
  and and_6 (and_6_out, Logical_Shift_Right_bool, 1'b1);
  and and_7 (and_7_out, and_5_out, bit_sortant_decallage_left_logic);
  and and_8 (and_8_out, and_6_out, bit_sortant_decallage_right_logic);
  or or_2 (Flags_Update_Mask[1], and_7_out, and_8_out);

  assign Flags_Update_Mask[0] = 1'b0;

  // Other names for the same wires on the sheet: C_Flag_Value = Flags_Update_Mask[1];
  //   Flag_Output[3:1] = Flags_Update_Mask[3:1]; Z_Flag_Value = Flags_Update_Mask[2];
  //   N_Flag_Value = Flags_Update_Mask[3]; output_for_RD[2:0] = Rd

  // Notes on the sheet:
  //   Note: ALU uses Rn register for shifts. Use Rn instead of Rm for shifts (immediate) here too
  //   Note 3: Imm32_Enable forces the use of the immediate for Rm register
  //   Note 2: MOV uses RSB ALU opcode with Imm8 reversed so that it is copied to output register
  //   Pull output low on Enable = 0
  //   only ADD and SUB use Rm
  //   Enable carry for SUB since it is reversed in ALU
  //   ALU will use Imm32 instead of Rm
endmodule
